# Fritzing sketch apache (saved by Fritzing 0.9.3b)

parts:
  Part1 = Arduino Uno (Rev3)
  S1 = H-Bridge with L298N
  BT1 = Bluetooth HC-06u [package=THT]
  BATT1 = LiPoly Battery (1300mAh)  # not connected
  920KV_Motor1 = DJI 920 KV Motor
  M1 = ESC
  M2 = DC Motor
  M3 = DC Motor
  VCC1 = Battery
  VCC2 = Battery block 9V

nets:
  N1: Part1.D8, S1.IN4
  N2: Part1.D10_PWM/SS, M1.pin_8
  N3: Part1.D11_PWM/MOSI, S1.ENB
  GND: Part1.GND, S1.GND, BT1.GND, M1.GND, VCC2.-
  N4: Part1.D2, S1.IN2
  N5: Part1.D3_PWM, S1.ENA
  N6: Part1.D4, S1.IN1
  N7: Part1.D5_PWM, BT1.RXD
  N8: Part1.D6_PWM, BT1.TXD
  N9: Part1.D7, S1.IN3
  5V: Part1.5V, BT1.VCC
  VIN: Part1.VIN, S1.5V
  N10: S1.12V, VCC1.+
  N11: S1.M1-01, M3.pin_2
  N12: S1.M1-02, M3.pin_1
  N13: S1.M2-01, M2.pin_2
  N14: S1.M2-02, M2.pin_1
  N15: 920KV_Motor1.w, M1.W
  N16: 920KV_Motor1.v, M1.V
  N17: 920KV_Motor1.u, M1.U

custom parts:
  H-Bridge with L298N: h-bridge
  Bluetooth HC-06u: Bluetooth HC-06 - face up, pins down 16.5mm x 37.5mm PCB
  LiPoly Battery (1300mAh): Lithium Ion Polymer Battery (1300mAh)
  DJI 920 KV Motor: DJI Brushless Outrunner 2212/920K Motor F330-550
